// Logisim project Atividade Avaliativa.circ as structural Verilog: 3 circuits, main circuit main
module main (
  input  A,
  input  B,
  input  C,
  input  D,
  output X
);

  wire and_1_out, and_2_out, and_3_out, and_4_out, and_5_out, not_1_out, not_2_out, not_3_out, not_4_out,
       or_1_out, or_2_out, or_3_out, or_4_out, or_5_out;

  not not_1 (not_1_out, A);
  not not_2 (not_2_out, B);
  not not_3 (not_3_out, C);
  not not_4 (not_4_out, D);
  or or_1 (or_1_out, not_1_out, not_2_out);
  or or_2 (or_2_out, not_1_out, not_3_out);
  or or_3 (or_3_out, not_1_out, not_4_out);
  or or_4 (or_4_out, not_3_out, not_4_out);
  and and_1 (and_1_out, not_2_out, not_4_out);
  and and_2 (and_2_out, or_1_out, or_2_out);
  and and_3 (and_3_out, or_1_out, or_3_out);
  and and_4 (and_4_out, or_1_out, or_4_out);
  buf and_5 (and_5_out, or_3_out);  // AND_Gate
  or or_5 (or_5_out, and_2_out, and_3_out, and_4_out, and_5_out, and_1_out);
  not not_5 (X, or_5_out);
endmodule

module Projeto (
  input  A,
  input  B,
  input  C,
  input  D,
  output X
);

  buf and_1 (X, A);  // AND_Gate
endmodule

module Main (
  input  A,
  input  B,
  input  C,
  input  D,
  output X
);

  wire and_1_out, and_2_out, and_3_out, and_4_out, and_5_out, not_1_out, not_2_out, not_3_out, not_4_out,
       or_1_out, or_2_out, or_3_out, or_4_out, or_5_out, or_6_out;

  not not_1 (not_1_out, A);
  not not_2 (not_2_out, B);
  not not_3 (not_3_out, C);
  not not_4 (not_4_out, D);
  or or_1 (or_1_out, A, B);
  or or_2 (or_2_out, A, C);
  or or_3 (or_3_out, A, D);
  or or_4 (or_4_out, not_4_out, not_3_out);
  or or_5 (or_5_out, not_2_out, not_1_out);
  and and_1 (and_1_out, or_1_out, or_2_out);
  and and_2 (and_2_out, or_1_out, or_3_out);
  and and_3 (and_3_out, or_1_out, or_4_out);
  and and_4 (and_4_out, or_3_out, or_4_out);
  and and_5 (and_5_out, or_4_out, or_5_out);
  or or_6 (or_6_out, and_1_out, and_2_out, and_3_out, and_4_out, and_5_out);
  not not_5 (X, or_6_out);
endmodule
